# Fritzing sketch 04 - Controlling Multiple LEDs (saved by Fritzing 0.9.1b)
breadboards: 1

parts:
  Parts1 = SparkFun RedBoard [part_number=DEV-12757]
  R1 = Resistor [tolerance=±5% resistance=330 package=THT]
  LED1 = LED - 5mm [color="Red (633nm)" package="5 mm [THT]"]
  LED2 = LED - 5mm [color="Red (633nm)" package="5 mm [THT]"]
  R2 = Resistor [tolerance=±5% resistance=330 package=THT]
  LED3 = LED - 5mm [color="Red (633nm)" package="5 mm [THT]"]
  LED5 = LED - 5mm [color="Red (633nm)" package="5 mm [THT]"]
  R3 = Resistor [tolerance=±5% resistance=330 package=THT]
  R4 = Resistor [tolerance=±5% resistance=330 package=THT]

nets:
  N1: Parts1.D10_PWM/SS, LED5.anode
  N2: Parts1.D11_PWM/MOSI, LED3.anode
  N3: Parts1.D12/MISO, LED1.anode
  N4: Parts1.D13/SCK, LED2.anode
  N5: Parts1.GND, R1.Pin_1, R2.Pin_1, R3.Pin_1, R4.Pin_1
  N6: R1.Pin_0, LED2.cathode
  N7: LED1.cathode, R2.Pin_0
  N8: LED3.cathode, R3.Pin_0
  N9: LED5.cathode, R4.Pin_0

custom parts:
  SparkFun RedBoard: At SparkFun we use many Arduinos and we’re always looking for the simplest, most stable one. Each board is a bit different and no one board has everything we want, so we decided to make our own version that combines all our favorite features. The RedBoard combines the simplicity of the UNO’s Optiboot bootloader (which is used in the Pro series), the stability of the FTDI (which we all missed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
