# Fritzing sketch 06 - RGB LED (saved by Fritzing 0.9.1b)
breadboards: 1

parts:
  Parts1 = SparkFun RedBoard [part_number=DEV-12757]
  R1 = Resistor [tolerance=±5% resistance=330 package=THT]
  LED1 = RGB LED (com. cathode, rgb) [package="5 mm [THT]"]
  R2 = Resistor [tolerance=±5% resistance=330 package=THT]
  R3 = Resistor [tolerance=±5% resistance=330 package=THT]

nets:
  N1: Parts1.D9_PWM, R3.Pin_1
  N2: Parts1.D10_PWM/SS, R2.Pin_1
  N3: Parts1.D11_PWM/MOSI, R1.Pin_1
  N4: R1.Pin_0, LED1.blue_anode
  N5: LED1.red_anode, R3.Pin_0
  N6: LED1.green_anode, R2.Pin_0

custom parts:
  SparkFun RedBoard: At SparkFun we use many Arduinos and we’re always looking for the simplest, most stable one. Each board is a bit different and no one board has everything we want, so we decided to make our own version that combines all our favorite features. The RedBoard combines the simplicity of the UNO’s Optiboot bootloader (which is used in the Pro series), the stability of the FTDI (which we all missed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
