# Fritzing sketch 09 - Potentiometer (saved by Fritzing 0.9.1b)
breadboards: 1

parts:
  Parts1 = SparkFun RedBoard [part_number=DEV-12757]
  R2 = TRIMPOT [package=3386u]

nets:
  N1: Parts1.A0, R2.WIPER
  N2: Parts1.5V, R2.CCW
  N3: Parts1.GND, R2.CW

custom parts:
  SparkFun RedBoard: At SparkFun we use many Arduinos and we’re always looking for the simplest, most stable one. Each board is a bit different and no one board has everything we want, so we decided to make our own version that combines all our favorite features. The RedBoard combines the simplicity of the UNO’s Optiboot bootloader (which is used in the Pro series), the stability of the FTDI (which we all missed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
