# Fritzing sketch 13 - DC Motor (saved by Fritzing 0.9.1b)
breadboards: 1

parts:
  Parts1 = SparkFun RedBoard [part_number=DEV-12757]
  U1 = TRANSISTOR_NPN_2 [package=to-92]
  R1 = Resistor [tolerance=±5% resistance=10k package=THT]
  D1 = Diode [package=diode-hv]
  M1 = DC Motor

nets:
  N1: Parts1.GND, U1.E
  N2: Parts1.D3_PWM, R1.Pin_0
  N3: Parts1.5V, D1.C, M1.pin_1
  N4: U1.C, M1.pin_2
  N5: U1.B, R1.Pin_1

custom parts:
  SparkFun RedBoard: At SparkFun we use many Arduinos and we’re always looking for the simplest, most stable one. Each board is a bit different and no one board has everything we want, so we decided to make our own version that combines all our favorite features. The RedBoard combines the simplicity of the UNO’s Optiboot bootloader (which is used in the Pro series), the stability of the FTDI (which we all missed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
