# Fritzing sketch 14 - Servo (saved by Fritzing 0.9.1b)
breadboards: 1

parts:
  Parts1 = SparkFun RedBoard [part_number=DEV-12757]
  J1 = Basic Servo

nets:
  N1: Parts1.D3_PWM, J1.pulse
  5V: Parts1.5V, J1.vcc
  GND: Parts1.GND, J1.gnd

custom parts:
  SparkFun RedBoard: At SparkFun we use many Arduinos and we’re always looking for the simplest, most stable one. Each board is a bit different and no one board has everything we want, so we decided to make our own version that combines all our favorite features. The RedBoard combines the simplicity of the UNO’s Optiboot bootloader (which is used in the Pro series), the stability of the FTDI (which we all missed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
