# Fritzing sketch 16 - MMA8452 Accelerometer (saved by Fritzing 0.9.1b)
breadboards: 1

parts:
  Parts1 = SparkFun RedBoard [part_number=DEV-12757]
  3-Axis_Accelerometer1 = 3-Axis Accelerometer Breakout - MMA8452Q

nets:
  N1: Parts1.A4/SDA, 3-Axis_Accelerometer1.SDA
  N2: Parts1.A5/SCL, 3-Axis_Accelerometer1.SCL
  3V3: Parts1.3V3, 3-Axis_Accelerometer1.3.3V
  GND: Parts1.GND, 3-Axis_Accelerometer1.GND

custom parts:
  SparkFun RedBoard: At SparkFun we use many Arduinos and we’re always looking for the simplest, most stable one. Each board is a bit different and no one board has everything we want, so we decided to make our own version that combines all our favorite features. The RedBoard combines the simplicity of the UNO’s Optiboot bootloader (which is used in the Pro series), the stability of the FTDI (which we all missed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
